# Fritzing sketch AtariPaddles (saved by Fritzing 0.9.6b)
breadboards: 1

parts:
  Part2 = Arduino Micro (Rev3)  # not connected
  S1 = Round Pushbutton
  S2 = Round Pushbutton
  R1 = Rotary Potentiometer (Large) [maximum_resistance=100kΩ package=THT]
  R2 = Rotary Potentiometer (Large) [maximum_resistance=100kΩ package=THT]
  X1 = DB9 Connector [package=db9]  # not connected
  X2 = DB9 Connector [package=db9]

nets:
  N1: S1.leg0, S2.leg0, X2.2
  N2: S1.leg1, X2.7
  N3: S2.leg1, X2.8
  N4: R1.wiper, X2.9
  N5: R1.leg2, X2.5
  N6: R2.wiper, X2.3
